# Fritzing sketch Radar con Arduino y Processing (saved by Fritzing 0.9.3b)
circuit board: 8.46667cm x 5.64444cm
breadboards: 1

parts:
  Componente1 = Arduino Uno (Rev3)
  J1 = Basic Servo
  hc-sr1 = hc-sr04

nets:
  N1: Componente1.D8, hc-sr1.Trig
  N2: Componente1.D9_PWM, hc-sr1.Echo
  GND: Componente1.GND, J1.gnd, hc-sr1.GND
  N3: Componente1.D2, J1.pulse
  VCC: Componente1.5V, J1.vcc, hc-sr1.VCC
